# Fritzing sketch circuit (saved by Fritzing 0.8.5b)
circuit board: 15.2cm x 6.4cm
breadboards: 1

parts:
  IC1 = IC, DIP package, 8 pins [chip_label=NE555]
  IC2 = IC, DIP package, 16 pins [chip_label=4017]
  C1 = Ceramic Capacitor [capacitance=1µF package="100 mil [THT, multilayer]"]
  C2 = Ceramic Capacitor [capacitance=100nF package="100 mil [THT, multilayer]"]
  R1 = Resistor [tolerance=±5% resistance=47k package=THT]
  R2 = Resistor [tolerance=±5% resistance=1k package=THT]
  P1 = Rotary Potentiometer (Small) [maximum_resistance=1mΩ package=THT]
  LED1 = LED - 5mm [color="Red (633nm)" package="5 mm [THT]"]
  LED2 = LED - 5mm [color="Red (633nm)" package="5 mm [THT]"]
  LED3 = LED - 5mm [color="Red (633nm)" package="5 mm [THT]"]
  LED4 = LED - 5mm [color="Red (633nm)" package="5 mm [THT]"]
  LED6 = LED - 5mm [color="Red (633nm)" package="5 mm [THT]"]
  LED7 = LED - 5mm [color="Red (633nm)" package="5 mm [THT]"]
  LED5 = LED - 5mm [color="Red (633nm)" package="5 mm [THT]"]
  LED8 = LED - 5mm [color="Red (633nm)" package="5 mm [THT]"]
  P2_1 = Rotary Potentiometer (Small) [maximum_resistance=100kΩ package=THT]
  R3_(8x) = Resistor [tolerance=±5% resistance=470 package=THT]
  R3_7 = Resistor [tolerance=±5% resistance=10k package=THT]
  R3_6 = Resistor [tolerance=±5% resistance=10k package=THT]
  R3_5 = Resistor [tolerance=±5% resistance=10k package=THT]
  R3_4 = Resistor [tolerance=±5% resistance=10k package=THT]
  R3_1 = Resistor [tolerance=±5% resistance=10k package=THT]
  R3_2 = Resistor [tolerance=±5% resistance=10k package=THT]
  R3_3 = Resistor [tolerance=±5% resistance=10k package=THT]
  P2_2 = Rotary Potentiometer (Small) [maximum_resistance=100kΩ package=THT]
  P2_3 = Rotary Potentiometer (Small) [maximum_resistance=100kΩ package=THT]
  P2_5 = Rotary Potentiometer (Small) [maximum_resistance=100kΩ package=THT]
  P2_4 = Rotary Potentiometer (Small) [maximum_resistance=100kΩ package=THT]
  P2_6 = Rotary Potentiometer (Small) [maximum_resistance=100kΩ package=THT]
  P2_(8x) = Rotary Potentiometer (Small) [maximum_resistance=100kΩ package=THT]
  P2_7 = Rotary Potentiometer (Small) [maximum_resistance=100kΩ package=THT]
  D1_1 = Rectifier Diode [part_number=1N4007 package="300 mil [THT]"]
  D1_2 = Rectifier Diode [part_number=1N4001 package="300 mil [THT]"]
  D1_3 = Rectifier Diode [part_number=1N4001 package="300 mil [THT]"]
  D1_4 = Rectifier Diode [part_number=1N4001 package="300 mil [THT]"]
  D1_7 = Rectifier Diode [part_number=1N4001 package="300 mil [THT]"]
  D1_5 = Rectifier Diode [part_number=1N4001 package="300 mil [THT]"]
  D1_6 = Rectifier Diode [part_number=1N4001 package="300 mil [THT]"]
  D1_(8x) = Rectifier Diode [part_number=1N4007 package="300 mil [THT]"]
  Q1 = NPN-Transistor [part_number=C547B package="TO92 [THT]"]
  R5 = Resistor [tolerance=±5% resistance=22k package=THT]
  R6 = Resistor [tolerance=±5% resistance=27k package=THT]
  R4 = Resistor [tolerance=±5% resistance=22k package=THT]
  R7 = Resistor [tolerance=±20% resistance=100k package=THT]
  IC3 = IC, DIP package, 18 pins [chip_label=ULN2804A]
  P3_7 = Rotary Potentiometer (Small) [maximum_resistance=100kΩ package=THT]
  P3_(8x) = Rotary Potentiometer (Small) [maximum_resistance=100kΩ package=THT]
  P3_6 = Rotary Potentiometer (Small) [maximum_resistance=100kΩ package=THT]
  P3_4 = Rotary Potentiometer (Small) [maximum_resistance=100kΩ package=THT]
  P3_5 = Rotary Potentiometer (Small) [maximum_resistance=100kΩ package=THT]
  P3_3 = Rotary Potentiometer (Small) [maximum_resistance=100kΩ package=THT]
  P3_2 = Rotary Potentiometer (Small) [maximum_resistance=100kΩ package=THT]
  P3_1 = Rotary Potentiometer (Small) [maximum_resistance=100kΩ package=THT]
  D2_(8x) = Rectifier Diode [part_number=1N4007 package="300 mil [THT]"]
  D2_6 = Rectifier Diode [part_number=1N4001 package="300 mil [THT]"]
  D2_5 = Rectifier Diode [part_number=1N4001 package="300 mil [THT]"]
  D2_7 = Rectifier Diode [part_number=1N4001 package="300 mil [THT]"]
  D2_4 = Rectifier Diode [part_number=1N4001 package="300 mil [THT]"]
  D2_3 = Rectifier Diode [part_number=1N4001 package="300 mil [THT]"]
  D2_2 = Rectifier Diode [part_number=1N4001 package="300 mil [THT]"]
  D2_1 = Rectifier Diode [part_number=1N4007 package="300 mil [THT]"]

nets:
  GND: IC1.pin1, IC2.pin8, IC2.pin13, C1.0, C2.0, R6.Pin_1, R7.Pin_1, IC3.pin9
  9V: IC1.pin2, IC1.pin4, IC1.pin6, IC1.pin8, IC2.pin16, C1.1, C2.1, R1.Pin_1, R2.Pin_0, P2_1.leg2, R3_(8x).Pin_1, R3_7.Pin_1, R3_6.Pin_1, R3_5.Pin_1, R3_4.Pin_1, R3_1.Pin_1, R3_2.Pin_1, R3_3.Pin_1, P2_2.leg2, P2_3.leg2, P2_5.leg2, P2_4.leg2, P2_6.leg2, P2_(8x).leg2, P2_7.leg2, Q1.C, P3_7.leg2, P3_(8x).leg2, P3_6.leg2, P3_4.leg2, P3_5.leg2, P3_3.leg2, P3_2.leg2, P3_1.leg2
  N1: IC1.pin3, IC2.pin14, P1.leg1, P1.wiper, R4.Pin_0, R7.Pin_0
  N2: IC1.pin7, R2.Pin_1
  N3: IC2.pin1, IC3.pin6
  N4: IC2.pin2, IC3.pin2
  N5: IC2.pin3, IC3.pin1
  N6: IC2.pin4, IC3.pin3
  N7: IC2.pin5, IC3.pin7
  N8: IC2.pin6, IC3.pin8
  N9: IC2.pin7, IC3.pin4
  N10: IC2.pin9, IC2.pin15
  N11: IC2.pin10, IC3.pin5
  N12: R1.Pin_0, P1.leg2
  N13: LED1.cathode, P2_1.leg1, IC3.pin18, P3_1.leg1
  N14: LED1.anode, R3_1.Pin_0
  N15: LED2.cathode, P2_2.leg1, IC3.pin17, P3_2.leg1
  N16: LED2.anode, R3_2.Pin_0
  N17: LED3.cathode, P2_3.leg1, IC3.pin16, P3_3.leg1
  N18: LED3.anode, R3_3.Pin_0
  N19: LED4.cathode, P2_4.leg1, IC3.pin15, P3_4.leg1
  N20: LED4.anode, R3_4.Pin_0
  N21: LED6.cathode, P2_6.leg1, IC3.pin13, P3_6.leg1
  N22: LED6.anode, R3_6.Pin_0
  N23: LED7.cathode, P2_7.leg1, IC3.pin12, P3_7.leg1
  N24: LED7.anode, R3_7.Pin_0
  N25: LED5.cathode, P2_5.leg1, IC3.pin14, P3_5.leg1
  N26: LED5.anode, R3_5.Pin_0
  N27: LED8.cathode, P2_(8x).leg1, IC3.pin11, P3_(8x).leg1
  N28: LED8.anode, R3_(8x).Pin_0
  N29: P2_1.wiper, D1_1.anode
  N30: P2_2.wiper, D1_2.anode
  N31: P2_3.wiper, D1_3.anode
  N32: P2_5.wiper, D1_5.anode
  N33: P2_4.wiper, D1_4.anode
  N34: P2_6.wiper, D1_6.anode
  N35: P2_(8x).wiper, D1_(8x).anode
  N36: P2_7.wiper, D1_7.anode
  CV1 Output: D1_1.cathode, D1_2.cathode, D1_3.cathode, D1_4.cathode, D1_7.cathode, D1_5.cathode, D1_6.cathode, D1_(8x).cathode
  N37: Q1.E, R5.Pin_0
  N38: Q1.B, R4.Pin_1
  Gate Output: R5.Pin_1, R6.Pin_0
  N39: P3_7.wiper, D2_7.anode
  N40: P3_(8x).wiper, D2_(8x).anode
  N41: P3_6.wiper, D2_6.anode
  N42: P3_4.wiper, D2_4.anode
  N43: P3_5.wiper, D2_5.anode
  N44: P3_3.wiper, D2_3.anode
  N45: P3_2.wiper, D2_2.anode
  N46: P3_1.wiper, D2_1.anode
  CV2 Output: D2_(8x).cathode, D2_6.cathode, D2_5.cathode, D2_7.cathode, D2_4.cathode, D2_3.cathode, D2_2.cathode, D2_1.cathode

notes:
  9V
  GND
  CV1
  CV2
  CV1 Pots
  CV2 Pots
  LEDs
  Tempo
  SuperOCHO
  dr. hupf engineering
